# Fritzing sketch 3-relays (saved by Fritzing 1.0.1rc)
circuit board: 6.48cm x 5.6264cm
breadboards: 1

parts:
  J1 = double row female pin header, 40 pins [form="♀ (female)"]
  U1 = Mini-360 DC-DC Buck converter [package=THT]
  J1_2 = Screw terminal - 2 pins [package=THT]

nets:
  N1: J1.pin38, U1.OUT-
  N2: J1.pin40, U1.OUT+
  N3: U1.IN-, J1_2.pin2
  N4: U1.IN+, J1_2.pin1

notes:
  Greenglass
  Simple Power Hat v0.1

custom parts:
  Mini-360 DC-DC Buck converter: Mini-360 DC-DC Buck converter. Tiny buck step down voltage converter, input voltage 4.75 to 23V output 1 to 17V adjustable. Available from ebay and the like.
